# Fritzing sketch USB Mouse circuit diagram (saved by Fritzing 0.9.3b)
breadboards: 1

parts:
  GY1 = MPU-6050 Board GY-521 [form="♀ (female)" package=THT]
  Part4 = Arduino Pro Micro (Clone)
  S3 = Round Pushbutton
  S4 = Round Pushbutton

nets:
  N1: GY1.pin1, Part4.VCC
  N2: GY1.pin2, Part4.GND, S3.leg1, S4.leg0
  N3: GY1.pin3, Part4.D3
  N4: GY1.pin4, Part4.D2
  N5: Part4.D10, S3.leg0
  N6: Part4.D16, S4.leg1

custom parts:
  MPU-6050 Board GY-521: Acelerometro y Giroscopio MPU-6050 Board GY-521
